// Logisim project MIPS_pipeline.circ as structural Verilog: 1 circuit, main circuit main
module main (
  input  RST,
  input  reg_dst,
  input  ALUsrc,
  input  branch,
  input  mem_to_reg,
  input  mem_write,
  input  [3:0] ALUop
);

  wire bit_extender_2_out, CLK, PCsrc;
  wire [4:0] alu_1_p4, EX_MEM_REG_DST_q, EX_MEM_ZERO_q, ID_EX_RD_q, ID_EX_RT_q, multiplexer_3_out,
       registerfile_1_p3;
  wire [31:0] adder_1_out, adder_2_out, alu_1_p5, bit_extender_1_out, EX_MEM_ALU_q, EX_MEM_B_q, EX_MEM_PC_q,
       ID_EX_A_q, ID_EX_B_q, ID_EX_PC_q, ID_EX_SIGEXT_q, IF_ID_MEMi_q, IF_ID_PC_q, MEM_WB_ALU_RESULT_q,
       MEM_WB_DATA_q, multiplexer_1_out, multiplexer_2_out, PC_q, ram_1_p5, registerfile_1_p1,
       registerfile_1_p6, registerfile_1_p7, risc_vprogramrom_1_p2, shifter_1_out;

  Register #(.width(32)) PC (.D(multiplexer_1_out), .en(1'b1), .clk(CLK), .Q(PC_q), .clr(RST));
  Clock u_CLK (.out(CLK));
  Adder #(.width(32)) adder_1 (.a(32'h4), .b(PC_q), .out(adder_1_out));  // open: cin, cout
  Multiplexer #(.width(32), .enable("false")) multiplexer_1 (
    .in0(adder_1_out), .in1(EX_MEM_PC_q), .out(multiplexer_1_out), .sel(PCsrc));
  // RISC_VProgramROM risc_vprogramrom_1: pin names not known; wires that end beside it: PC_q, risc_vprogramrom_1_p2, IF_ID_MEMi_q[31:26]
  Register #(.width(32)) IF_ID_PC (.D(adder_1_out), .en(1'b1), .clk(CLK), .Q(IF_ID_PC_q), .clr(RST));
  Register #(.width(32)) IF_ID_MEMi (.D(risc_vprogramrom_1_p2), .en(1'b1), .clk(CLK), .Q(IF_ID_MEMi_q), .clr(RST));
  // RegisterFile registerfile_1: pin names not known; wires that end beside it: registerfile_1_p1, 1'b1, registerfile_1_p3, IF_ID_MEMi_q[25:21], IF_ID_MEMi_q[20:16], registerfile_1_p6, registerfile_1_p7
  assign bit_extender_1_out = {{16{IF_ID_MEMi_q[15]}}, IF_ID_MEMi_q[15:0]};  // Bit_Extender bit_extender_1
  Register #(.width(32)) ID_EX_PC (.D(IF_ID_PC_q), .en(1'b1), .clk(CLK), .Q(ID_EX_PC_q), .clr(RST));
  Register #(.width(32)) ID_EX_A (.D(registerfile_1_p6), .en(1'b1), .clk(CLK), .Q(ID_EX_A_q), .clr(RST));
  Register #(.width(32)) ID_EX_B (.D(registerfile_1_p7), .en(1'b1), .clk(CLK), .Q(ID_EX_B_q), .clr(RST));
  Register #(.width(32)) ID_EX_SIGEXT (.D(bit_extender_1_out), .en(1'b1), .clk(CLK), .Q(ID_EX_SIGEXT_q), .clr(RST));
  Register #(.width(5)) ID_EX_RD (.D(IF_ID_MEMi_q[15:11]), .en(1'b1), .clk(CLK), .Q(ID_EX_RD_q), .clr(RST));
  Register #(.width(5)) ID_EX_RT (.D(IF_ID_MEMi_q[25:21]), .en(1'b1), .clk(CLK), .Q(ID_EX_RT_q), .clr(RST));
  Multiplexer #(.width(32), .enable("false")) multiplexer_2 (
    .in0(ID_EX_B_q), .in1(ID_EX_SIGEXT_q), .out(multiplexer_2_out), .sel(ALUsrc));
  Shifter #(.width(32)) shifter_1 (.in(ID_EX_SIGEXT_q), .\dist (5'b00010), .out(shifter_1_out));
  // ALU alu_1: pin names not known; wires that end beside it: ID_EX_A_q, multiplexer_2_out, ALUop, alu_1_p4, alu_1_p5
  Adder #(.width(32)) adder_2 (.a(ID_EX_PC_q), .b(shifter_1_out), .out(adder_2_out));  // open: cin, cout
  Multiplexer #(.width(5), .enable("false")) multiplexer_3 (
    .in0(ID_EX_RD_q), .in1(ID_EX_RT_q), .out(multiplexer_3_out), .sel(reg_dst));
  Register #(.width(32)) EX_MEM_PC (.D(adder_2_out), .en(1'b1), .clk(CLK), .Q(EX_MEM_PC_q), .clr(RST));
  Register #(.width(32)) EX_MEM_B (.D(ID_EX_B_q), .en(1'b1), .clk(CLK), .Q(EX_MEM_B_q), .clr(RST));
  Register #(.width(32)) EX_MEM_ALU (.D(alu_1_p5), .en(1'b1), .clk(CLK), .Q(EX_MEM_ALU_q), .clr(RST));
  Register #(.width(5)) EX_MEM_ZERO (.D(alu_1_p4), .en(1'b1), .clk(CLK), .Q(EX_MEM_ZERO_q), .clr(RST));
  Register #(.width(5)) EX_MEM_REG_DST (.D(multiplexer_3_out), .en(1'b1), .clk(CLK), .Q(EX_MEM_REG_DST_q), .clr(RST));
  Bit_Extender #(.in_width(5), .out_width(1)) bit_extender_2 (.in(EX_MEM_ZERO_q), .out(bit_extender_2_out));
  and and_1 (PCsrc, branch, bit_extender_2_out);
  // RAM ram_1: pin names not known; wires that end beside it: EX_MEM_ALU_q[19:0], EX_MEM_B_q, CLK, RST, ram_1_p5
  Register #(.width(32)) MEM_WB_ALU_RESULT (.D(EX_MEM_ALU_q), .en(1'b1), .clk(CLK), .Q(MEM_WB_ALU_RESULT_q), .clr(RST));
  Register #(.width(32)) MEM_WB_DATA (.D(ram_1_p5), .en(1'b1), .clk(CLK), .Q(MEM_WB_DATA_q), .clr(RST));
  Register #(.width(5)) MEM_WB_REG_DST (.D(EX_MEM_REG_DST_q), .en(1'b1), .clk(CLK), .Q(registerfile_1_p3), .clr(RST));
  Multiplexer #(.width(32), .enable("false")) multiplexer_4 (
    .in0(MEM_WB_ALU_RESULT_q), .in1(MEM_WB_DATA_q), .out(registerfile_1_p1), .sel(mem_to_reg));
endmodule
